// Logisim project Custom x16 processor.circ as structural Verilog
module main (
  input  in_1,
  input  in_2,
  input  in_3,
  input  in_4,
  output out_5,
  output Carry,
  output Fa1,
  output S
);

  // FAopt1 faopt1_1: pin names not known; wires that end beside it: Carry, in_1, S, in_2
  // FA1 fa1_1: pin names not known; wires that end beside it: out_5, in_3, Fa1, in_4
endmodule

module FAopt1 (
  input  in_1,
  input  in_2,
  input  Carry,
  output _4_75,
  output S
);

  wire _0_75_2_out, _0_75_3_out, _0_75_4_out, _0_75_out, _1_2_out, _1_3_out, _1_4_out, _1_6_out, _1_7_out,
       _1_8_out, _1_out;

  not _0_75 (_0_75_out, in_1);
  not _0_75_2 (_0_75_2_out, in_2);
  nand _1 (_1_out, _1_6_out, Carry);
  nand _1_2 (_1_2_out, in_1, in_2);
  nand _1_3 (_1_3_out, _0_75_out, in_2);
  nand _1_4 (_1_4_out, in_1, _0_75_2_out);
  nand _1_5 (_4_75, _1_out, _1_2_out);
  nand _1_6 (_1_6_out, _1_3_out, _1_4_out);
  not _0_75_3 (_0_75_3_out, Carry);
  not _0_75_4 (_0_75_4_out, _1_6_out);
  nand _1_7 (_1_7_out, _0_75_4_out, Carry);
  nand _1_8 (_1_8_out, _1_6_out, _0_75_3_out);
  nand _1_9 (S, _1_7_out, _1_8_out);

  // Notes on the sheet:
  //   Carry Bit
  //   5.5
endmodule

module FA1 (
  input  in_1,
  input  in_2,
  output Carry,
  output Sum
);

  wire nand_1_out;

  or or_1 (Carry, in_1, in_2);
  nand nand_1 (nand_1_out, in_1, in_2);
  nand nand_2 (Sum, Carry, nand_1_out);
endmodule

module Full_Adder (
  input  in_1,
  input  in_2,
  input  in_3,
  output Sum,
  output Carry
);

  wire _16_out, nand_1_out, nand_2_out, nand_3_out;

  xor _16 (_16_out, in_1, in_2);
  xor _16_2 (Sum, _16_out, in_3);
  nand nand_1 (nand_1_out, in_1, in_2);
  nand nand_2 (nand_2_out, in_2, in_3);
  nand nand_3 (nand_3_out, in_3, in_1);
  nand nand_4 (Carry, nand_1_out, nand_2_out, nand_3_out);
endmodule

module FA_opt_2 (
  input  in_1,
  input  in_2,
  input  Carry,
  output Carry_Bit,
  output _5_5
);

  wire _1_2_out, _1_3_out, _1_5_out, _1_6_out, _1_7_out, _1_8_out, _1_9_out, _1_out, not_1_out, not_2_out,
       not_3_out, not_4_out;

  nand _1 (_1_out, in_1, in_2);
  nand _1_2 (_1_2_out, in_2, Carry);
  nand _1_3 (_1_3_out, Carry, in_1);
  not not_1 (not_1_out, in_1);
  not not_2 (not_2_out, in_2);
  nand _1_4 (Carry_Bit, _1_out, _1_2_out, _1_3_out);
  nand _1_5 (_1_5_out, not_1_out, in_2);
  nand _1_6 (_1_6_out, in_1, not_2_out);
  nand _1_7 (_1_7_out, _1_5_out, _1_6_out);
  not not_3 (not_3_out, _1_7_out);
  not not_4 (not_4_out, Carry);
  nand _1_8 (_1_8_out, not_3_out, Carry);
  nand _1_9 (_1_9_out, _1_7_out, not_4_out);
  nand _1_10 (_5_5, _1_8_out, _1_9_out);

  // Notes on the sheet:
  //   .75
  //   .751
  //   2
  //   .75
  //   .75
endmodule

module ripple (
  input  [3:0] in_1,
  input  [3:0] in_2,
  output _8,
  output [3:0] _8_75
);

  wire fa0_1_carry, FAo2_carry_bit, faopt1_1__4_75;

  FAopt1 _75 (.in_1(faopt1_1__4_75), .in_2(in_1[3]), .Carry(in_2[3]), .S(_8_75[3]), ._4_75(_8));
  FAopt1 faopt1_1 (.in_1(FAo2_carry_bit), .in_2(in_1[2]), .Carry(in_2[2]), .S(_8_75[2]), ._4_75(faopt1_1__4_75));
  FA_opt_2 FAo2 (.in_1(fa0_1_carry), .in_2(in_1[1]), .Carry(in_2[1]), .Carry_Bit(FAo2_carry_bit), ._5_5(_8_75[1]));
  FA0 fa0_1 (.in_1(in_1[0]), .in_2(in_2[0]), .Out(_8_75[0]), .Carry(fa0_1_carry));

  // Notes on the sheet:
  //   2
  //   Carry
  //   4.75
  //   .75
  //   5.5
  //   1.75
  //   2
endmodule

module _4to1_Mux (
  input  SEL,
  input  in_2,
  input  in_3,
  output Total_2_75
);

  wire _75_out, nand_1_out, nand_2_out;

  not _75 (_75_out, SEL);
  nand nand_1 (nand_1_out, in_2, _75_out);
  nand nand_2 (nand_2_out, SEL, in_3);
  nand nand_3 (Total_2_75, nand_1_out, nand_2_out);

  // Notes on the sheet:
  //   1(for both)
  //   1
endmodule

module _4_to_1_actually_a_4_1 (
  input  in_1,
  input  in_2,
  input  in_3,
  input  in_4,
  input  in_5,
  input  in_6,
  output out_7
);

  wire n4to1_mux_1_total_2_75, n4to1_mux_2_total_2_75;

  _4to1_Mux u_4to1_mux_1 (.SEL(in_6), .in_2(in_1), .in_3(in_2), .Total_2_75(n4to1_mux_1_total_2_75));
  _4to1_Mux u_4to1_mux_2 (.SEL(in_6), .in_2(in_3), .in_3(in_4), .Total_2_75(n4to1_mux_2_total_2_75));
  _4to1_Mux u_4to1_mux_3 (.SEL(in_5), .in_2(n4to1_mux_1_total_2_75), .in_3(n4to1_mux_2_total_2_75), .Total_2_75(out_7));

  // Notes on the sheet:
  //   Each is 2.75
  //   Total=5ns
endmodule

module _2_1_mux__2 (
  input  _0,
  input  _1,
  input  Sel_1,
  output \output 
);

  wire not_1_out, transmission_1_p4;

  not not_1 (not_1_out, Sel_1);
  // Transmission_Gate transmission_1: pin names not known; wires that end beside it: _0, Sel_1, not_1_out, transmission_1_p4
  not not_2 (\output , transmission_1_p4);
  // Transmission_Gate transmission_2: pin names not known; wires that end beside it: _1, not_1_out, Sel_1, transmission_1_p4

  // Notes on the sheet:
  //   .25
  //   .75
  //   .25
  //   .75
  //   Total=1.75
endmodule

module _4_1_mux__2_inv (
  input  in_1,
  input  in_2,
  input  _1_75,
  input  in_4,
  input  in_5,
  input  in_6,
  output Output
);

  wire n2_1_mux_2_1_output, n2_1_mux_2_2_output;

  _2_1_mux__2 u_2_1_mux_2_1 (._0(in_1), ._1(in_2), .Sel_1(in_6), .\output (n2_1_mux_2_1_output));
  _2_1_mux__2 u_2_1_mux_2_2 (._0(_1_75), ._1(in_4), .Sel_1(in_6), .\output (n2_1_mux_2_2_output));
  _2_1_mux__2 u_2_1_mux_2_3 (._0(n2_1_mux_2_1_output), ._1(n2_1_mux_2_2_output), .Sel_1(in_5), .\output (Output));

  // Notes on the sheet:
  //   1.75
  //   1.75
  //   Total=3.5
endmodule

module _8bit_carry_select_adder (
  input  [7:0] in_1,
  input  [7:0] in_2,
  output [7:0] _11_25,
  output Carry
);

  wire _1_75_output, ripple1_1__8, ripple_1__8, ripple_2__8;
  wire [3:0] _1_75_2_out_4, ripple1_1__8_75, ripple_1__8_75;

  _2_1_mux__2 _1_75 (._0(ripple_1__8), ._1(ripple1_1__8), .Sel_1(ripple_2__8), .\output (_1_75_output));
  ripple1 ripple1_1 (.in_1(in_1[7:4]), .in_2(in_2[7:4]), ._8(ripple1_1__8), ._8_75(ripple1_1__8_75));  // open: out_5
  not not_1 (Carry, _1_75_output);
  ripple ripple_1 (.in_1(in_1[7:4]), .in_2(in_2[7:4]), ._8(ripple_1__8), ._8_75(ripple_1__8_75));
  _2_1_mux_i__3_0 _1_75_2 (.a(ripple_1__8_75), .b(ripple1_1__8_75), .carry(ripple_2__8), .out_4(_1_75_2_out_4));
  ripple ripple_2 (.in_1(in_1[3:0]), .in_2(in_2[3:0]), ._8(ripple_2__8), ._8_75(_11_25[3:0]));
  assign _11_25[7:4] = ~_1_75_2_out_4;  // NOT_Gate not_2, 4 bits wide

  // Notes on the sheet:
  //   8
  //   8.75
  //   .75
  //   10.5
  //   8
  //   8.75
  //   8
  //   8.75
  //   .75
endmodule

module FA0 (
  input  in_1,
  input  in_2,
  output Out,
  output Carry
);

  wire _1_out;

  nor _1 (_1_out, in_1, in_2);
  and _1_75 (Carry, in_1, in_2);
  nor _1_2 (Out, _1_out, Carry);
endmodule

module _8_bit_ripple_adder (
  input  [7:0] _0,
  input  [7:0] _0_2,
  output Carry,
  output [7:0] _16_75
);

  wire fa0_1_carry, fa_opt_2_1_carry_bit, full_adder_2_carry, full_adder_3_carry, full_adder_4_carry,
       full_adder_5_carry, full_adder_6_carry;

  Full_Adder full_adder_1 (.in_1(_0_2[7]), .in_2(_0[7]), .in_3(full_adder_2_carry), .Sum(_16_75[7]), .Carry(Carry));
  Full_Adder full_adder_2 (
    .in_1(_0_2[6]), .in_2(_0[6]), .in_3(full_adder_3_carry), .Sum(_16_75[6]), .Carry(full_adder_2_carry));
  Full_Adder full_adder_3 (
    .in_1(_0_2[5]), .in_2(_0[5]), .in_3(full_adder_5_carry), .Sum(_16_75[5]), .Carry(full_adder_3_carry));
  Full_Adder full_adder_4 (
    .in_1(_0_2[3]), .in_2(_0[3]), .in_3(full_adder_6_carry), .Sum(_16_75[3]), .Carry(full_adder_4_carry));
  Full_Adder full_adder_5 (
    .in_1(_0_2[4]), .in_2(_0[4]), .in_3(full_adder_4_carry), .Sum(_16_75[4]), .Carry(full_adder_5_carry));
  Full_Adder full_adder_6 (
    .in_1(_0_2[2]), .in_2(_0[2]), .in_3(fa_opt_2_1_carry_bit), .Sum(_16_75[2]), .Carry(full_adder_6_carry));
  FA_opt_2 fa_opt_2_1 (
    .in_1(_0[1]), .in_2(_0_2[1]), .Carry(fa0_1_carry), .Carry_Bit(fa_opt_2_1_carry_bit), ._5_5(_16_75[1]));
  FA0 fa0_1 (.in_1(_0[0]), .in_2(_0_2[0]), .Out(_16_75[0]), .Carry(fa0_1_carry));

  // Notes on the sheet:
  //   16
  //   16
  //   14
  //   12
  //   14.75
  //   16.75
  //   10
  //   12.75
  //   8
  //   10.75
  //   8.75
  //   6
  //   4
  //   6.75
  //   1.75
  //   5.5
  //   2
endmodule

module ripple1 (
  input  [3:0] in_1,
  input  [3:0] in_2,
  output _8,
  output [3:0] _8_75,
  output out_5
);

  wire fa1_1_carry, FAo2_carry_bit;

  FAopt1 _75 (.in_1(out_5), .in_2(in_1[3]), .Carry(in_2[3]), .S(_8_75[3]), ._4_75(_8));
  FAopt1 faopt1_1 (.in_1(FAo2_carry_bit), .in_2(in_1[2]), .Carry(in_2[2]), .S(_8_75[2]), ._4_75(out_5));
  FA_opt_2 FAo2 (.in_1(fa1_1_carry), .in_2(in_1[1]), .Carry(in_2[1]), .Carry_Bit(FAo2_carry_bit), ._5_5(_8_75[1]));
  FA1 fa1_1 (.in_1(in_2[0]), .in_2(in_1[0]), .Carry(fa1_1_carry), .Sum(_8_75[0]));

  // Notes on the sheet:
  //   2
  //   Carry
  //   4.75
  //   .75
  //   2nd to last carry
  //   5.5
  //   1.75
  //   2
endmodule

module _4_wide_2_1_mux (
  input  [3:0] A,
  input  [3:0] B,
  input  Carry,
  output [3:0] out_4
);

  _4to1_Mux u_4to1_mux_1 (.SEL(Carry), .in_2(A[0]), .in_3(B[0]), .Total_2_75(out_4[0]));
  _4to1_Mux u_4to1_mux_2 (.SEL(Carry), .in_2(A[1]), .in_3(B[1]), .Total_2_75(out_4[1]));
  _4to1_Mux u_4to1_mux_3 (.SEL(Carry), .in_2(A[2]), .in_3(B[2]), .Total_2_75(out_4[2]));
  _4to1_Mux u_4to1_mux_4 (.SEL(Carry), .in_2(A[3]), .in_3(B[3]), .Total_2_75(out_4[3]));
endmodule

module _2_1_mux_i__3_0 (
  input  [3:0] a,
  input  [3:0] b,
  input  carry,
  output [3:0] out_4
);

  _2_1_mux__2 u_2_1_mux_2_1 (._0(a[0]), ._1(b[0]), .Sel_1(carry), .\output (out_4[0]));
  _2_1_mux__2 u_2_1_mux_2_2 (._0(a[1]), ._1(b[1]), .Sel_1(carry), .\output (out_4[1]));
  _2_1_mux__2 u_2_1_mux_2_3 (._0(a[2]), ._1(b[2]), .Sel_1(carry), .\output (out_4[2]));
  _2_1_mux__2 u_2_1_mux_2_4 (._0(a[3]), ._1(b[3]), .Sel_1(carry), .\output (out_4[3]));
endmodule

module _8bit_carry_select_adder_1 (
  input  [7:0] in_1,
  input  [7:0] in_2,
  output [7:0] _11_25,
  output Carry,
  output out_5
);

  wire _1_75_output, ripple1_1__8, ripple1_2__8, ripple_1__8;
  wire [3:0] _1_75_2_out_4, ripple1_1__8_75, ripple_1__8_75;

  _2_1_mux__2 _1_75 (._0(ripple_1__8), ._1(ripple1_1__8), .Sel_1(ripple1_2__8), .\output (_1_75_output));
  ripple1 ripple1_1 (.in_1(in_1[7:4]), .in_2(in_2[7:4]), ._8(ripple1_1__8), ._8_75(ripple1_1__8_75), .out_5(out_5));
  not not_1 (Carry, _1_75_output);
  ripple ripple_1 (.in_1(in_1[7:4]), .in_2(in_2[7:4]), ._8(ripple_1__8), ._8_75(ripple_1__8_75));
  _2_1_mux_i__3_0 _1_75_2 (.a(ripple_1__8_75), .b(ripple1_1__8_75), .carry(ripple1_2__8), .out_4(_1_75_2_out_4));
  assign _11_25[7:4] = ~_1_75_2_out_4;  // NOT_Gate not_2, 4 bits wide
  ripple1 ripple1_2 (.in_1(in_1[3:0]), .in_2(in_2[3:0]), ._8(ripple1_2__8), ._8_75(_11_25[3:0]));  // open: out_5

  // Notes on the sheet:
  //   8
  //   8.75
  //   .75
  //   10.5
  //   8
  //   8.75
  //   2nd to last carry
  //   8
  //   8.75
  //   .75
endmodule

module _16_bit_ripple_carry (
  input  [15:0] in_1,
  input  [15:0] in_2,
  output [15:0] _13_75,
  output Carry,
  output _2nd_to_last
);

  wire _1_75_output, n8bit_carry_select_adder_1_1_carry, n8bit_carry_select_adder_1_carry,
       n8bit_carry_select_adder_2_carry;
  wire [7:0] n8_1_mux_i_7_0_1_out_4, n8bit_carry_select_adder_1_1__11_25, n8bit_carry_select_adder_1__11_25;

  _2_1_mux__2 _1_75 (
    ._0(n8bit_carry_select_adder_1_carry), ._1(n8bit_carry_select_adder_1_1_carry),
    .Sel_1(n8bit_carry_select_adder_2_carry), .\output (_1_75_output));
  _8bit_carry_select_adder_1 u_8bit_carry_select_adder_1_1 (
    .in_1(in_2[15:8]), .in_2(in_1[15:8]), ._11_25(n8bit_carry_select_adder_1_1__11_25),
    .Carry(n8bit_carry_select_adder_1_1_carry), .out_5(_2nd_to_last));
  not not_1 (Carry, _1_75_output);
  _8_1_mux_i__7_0 u_8_1_mux_i_7_0_1 (
    .in_1(n8bit_carry_select_adder_1__11_25), .in_2(n8bit_carry_select_adder_1_1__11_25),
    .in_3(n8bit_carry_select_adder_2_carry), .out_4(n8_1_mux_i_7_0_1_out_4));
  _8bit_carry_select_adder u_8bit_carry_select_adder_1 (
    .in_1(in_1[15:8]), .in_2(in_2[15:8]), ._11_25(n8bit_carry_select_adder_1__11_25),
    .Carry(n8bit_carry_select_adder_1_carry));
  assign _13_75[15:8] = ~n8_1_mux_i_7_0_1_out_4;  // NOT_Gate not_2, 8 bits wide
  _8bit_carry_select_adder u_8bit_carry_select_adder_2 (
    .in_1(in_1[7:0]), .in_2(in_2[7:0]), ._11_25(_13_75[7:0]), .Carry(n8bit_carry_select_adder_2_carry));

  // Notes on the sheet:
  //   11.25
  //   .75
  //   13
  //   THIS IS ACTUALLY CARRY SELECT
  //   8
  //   8.75
  //   11.25
  //   .75
  //   11.25
endmodule

module _8_1_mux_i__7_0 (
  input  [7:0] in_1,
  input  [7:0] in_2,
  input  in_3,
  output [7:0] out_4
);

  _2_1_mux_i__3_0 u_2_1_mux_i_3_0_1 (.a(in_1[3:0]), .b(in_2[3:0]), .carry(in_3), .out_4(out_4[3:0]));
  _2_1_mux_i__3_0 u_2_1_mux_i_3_0_2 (.a(in_1[7:4]), .b(in_2[7:4]), .carry(in_3), .out_4(out_4[7:4]));
endmodule

module _4bit_carrry_select_add_subtract (
  input  [3:0] A,
  input  [3:0] B,
  input  OP,
  output _8,
  output Overflow,
  output [3:0] _8_75
);

  wire FAo2_carry_bit, faopt1_1__4_75, faopt1_2__4_75, xor_2_out, xor_3_out, xor_4_out, xor_5_out;

  xor xor_1 (Overflow, _8, faopt1_1__4_75);
  xor xor_2 (xor_2_out, OP, B[3]);
  FAopt1 _75 (.in_1(faopt1_1__4_75), .in_2(A[3]), .Carry(xor_2_out), .S(_8_75[3]), ._4_75(_8));
  xor xor_3 (xor_3_out, OP, B[2]);
  FAopt1 faopt1_1 (.in_1(faopt1_2__4_75), .in_2(A[2]), .Carry(xor_3_out), .S(_8_75[2]), ._4_75(faopt1_1__4_75));
  xor xor_4 (xor_4_out, OP, B[0]);
  xor xor_5 (xor_5_out, OP, B[1]);
  FAopt1 faopt1_2 (.in_1(FAo2_carry_bit), .in_2(A[1]), .Carry(xor_5_out), .S(_8_75[1]), ._4_75(faopt1_2__4_75));
  FA_opt_2 FAo2 (.in_1(A[0]), .in_2(xor_4_out), .Carry(OP), .Carry_Bit(FAo2_carry_bit), ._5_5(_8_75[0]));

  // Notes on the sheet:
  //   2
  //   Carry
  //   4.75
  //   .75
  //   5.5
  //   Carry in
  //   2
endmodule

module _16bit_car_sel_add_more (
  input  [15:0] in_1,
  input  [15:0] in_2,
  input  Carry_In,
  output [15:0] _13_75,
  output Carry,
  output out_6
);

  wire _1_75_output, n8bit_car_sel_full_1_carry, n8bit_carry_select_adder_1_1_carry,
       n8bit_carry_select_adder_1_carry;
  wire [7:0] n8_1_mux_i_7_0_1_out_4, n8bit_carry_select_adder_1_1__11_25, n8bit_carry_select_adder_1__11_25;

  _2_1_mux__2 _1_75 (
    ._0(n8bit_carry_select_adder_1_carry), ._1(n8bit_carry_select_adder_1_1_carry),
    .Sel_1(n8bit_car_sel_full_1_carry), .\output (_1_75_output));
  _8bit_carry_select_adder_1 u_8bit_carry_select_adder_1_1 (
    .in_1(in_2[15:8]), .in_2(in_1[15:8]), ._11_25(n8bit_carry_select_adder_1_1__11_25),
    .Carry(n8bit_carry_select_adder_1_1_carry), .out_5(out_6));
  not not_1 (Carry, _1_75_output);
  _8_1_mux_i__7_0 u_8_1_mux_i_7_0_1 (
    .in_1(n8bit_carry_select_adder_1__11_25), .in_2(n8bit_carry_select_adder_1_1__11_25),
    .in_3(n8bit_car_sel_full_1_carry), .out_4(n8_1_mux_i_7_0_1_out_4));
  _8bit_carry_select_adder u_8bit_carry_select_adder_1 (
    .in_1(in_1[15:8]), .in_2(in_2[15:8]), ._11_25(n8bit_carry_select_adder_1__11_25),
    .Carry(n8bit_carry_select_adder_1_carry));
  assign _13_75[15:8] = ~n8_1_mux_i_7_0_1_out_4;  // NOT_Gate not_2, 8 bits wide
  _8bit_car_sel_full u_8bit_car_sel_full_1 (
    .in_1(in_2[7:0]), .in_2(in_1[7:0]), ._11_25(_13_75[7:0]), .Carry(n8bit_car_sel_full_1_carry),
    .Carry_IN(Carry_In));

  // Notes on the sheet:
  //   11.25
  //   .75
  //   13
  //   8
  //   8.75
  //   11.25
  //   2nd to last carry
  //   .75
endmodule

module _16bit_car_sel_add_sub (
  input  [15:0] in_1,
  input  OP,
  input  [15:0] in_3,
  output Overflow,
  output [15:0] out_5
);

  wire n16bit_car_sel_add_more_1_carry, n16bit_car_sel_add_more_1_out_6;
  wire [15:0] thanks_lojisim_1_out_3;

  xor xor_1 (Overflow, n16bit_car_sel_add_more_1_carry, n16bit_car_sel_add_more_1_out_6);
  thanks_lojisim thanks_lojisim_1 (.in_2(in_1), .in_1(OP), .out_3(thanks_lojisim_1_out_3));
  _16bit_car_sel_add_more u_16bit_car_sel_add_more_1 (
    .in_1(in_3), .in_2(thanks_lojisim_1_out_3), ._13_75(out_5), .Carry(n16bit_car_sel_add_more_1_carry),
    .out_6(n16bit_car_sel_add_more_1_out_6), .Carry_In(OP));

  // Notes on the sheet:
  //   A
  //   B (orig)
  //   Output
endmodule

module thanks_lojisim (
  input  in_1,
  input  [15:0] in_2,
  output [15:0] out_3
);

  assign out_3 = in_2 ^ {16{in_1}};  // XOR_Gate xor_1, 16 bits wide

  // Notes on the sheet:
  //   THANKS LOGISIM!
endmodule

module _16bit_car_sel_norm (
  input  [15:0] in_1,
  input  [15:0] in_2,
  output [15:0] _13_75,
  output Carry
);

  wire _1_75_output, n8bit_carry_select_adder_1_1_carry, n8bit_carry_select_adder_1_carry,
       n8bit_carry_select_adder_2_carry;
  wire [7:0] n8_1_mux_i_7_0_1_out_4, n8bit_carry_select_adder_1_1__11_25, n8bit_carry_select_adder_1__11_25;

  _2_1_mux__2 _1_75 (
    ._0(n8bit_carry_select_adder_1_carry), ._1(n8bit_carry_select_adder_1_1_carry),
    .Sel_1(n8bit_carry_select_adder_2_carry), .\output (_1_75_output));
  _8bit_carry_select_adder_1 u_8bit_carry_select_adder_1_1 (
    .in_1(in_2[15:8]), .in_2(in_1[15:8]), ._11_25(n8bit_carry_select_adder_1_1__11_25),
    .Carry(n8bit_carry_select_adder_1_1_carry));  // open: out_5
  not not_1 (Carry, _1_75_output);
  _8_1_mux_i__7_0 u_8_1_mux_i_7_0_1 (
    .in_1(n8bit_carry_select_adder_1__11_25), .in_2(n8bit_carry_select_adder_1_1__11_25),
    .in_3(n8bit_carry_select_adder_2_carry), .out_4(n8_1_mux_i_7_0_1_out_4));
  _8bit_carry_select_adder u_8bit_carry_select_adder_1 (
    .in_1(in_1[15:8]), .in_2(in_2[15:8]), ._11_25(n8bit_carry_select_adder_1__11_25),
    .Carry(n8bit_carry_select_adder_1_carry));
  assign _13_75[15:8] = ~n8_1_mux_i_7_0_1_out_4;  // NOT_Gate not_2, 8 bits wide
  _8bit_carry_select_adder u_8bit_carry_select_adder_2 (
    .in_1(in_1[7:0]), .in_2(in_2[7:0]), ._11_25(_13_75[7:0]), .Carry(n8bit_carry_select_adder_2_carry));

  // Notes on the sheet:
  //   11.25
  //   .75
  //   13
  //   8
  //   8.75
  //   11.25
  //   .75
  //   11.25
endmodule

module _8bit_car_sel_full (
  input  [7:0] in_1,
  input  [7:0] in_2,
  input  Carry_IN,
  output [7:0] _11_25,
  output Carry
);

  wire _1_75_output, n4_bit_full_adder_1__8, ripple1_1__8, ripple_1__8;
  wire [3:0] _1_75_2_out_4, ripple1_1__8_75, ripple_1__8_75;

  _2_1_mux__2 _1_75 (._0(ripple_1__8), ._1(ripple1_1__8), .Sel_1(n4_bit_full_adder_1__8), .\output (_1_75_output));
  ripple1 ripple1_1 (.in_1(in_1[7:4]), .in_2(in_2[7:4]), ._8(ripple1_1__8), ._8_75(ripple1_1__8_75));  // open: out_5
  not not_1 (Carry, _1_75_output);
  ripple ripple_1 (.in_1(in_1[7:4]), .in_2(in_2[7:4]), ._8(ripple_1__8), ._8_75(ripple_1__8_75));
  _2_1_mux_i__3_0 _1_75_2 (
    .a(ripple_1__8_75), .b(ripple1_1__8_75), .carry(n4_bit_full_adder_1__8), .out_4(_1_75_2_out_4));
  assign _11_25[7:4] = ~_1_75_2_out_4;  // NOT_Gate not_2, 4 bits wide
  _4_bit_full_adder u_4_bit_full_adder_1 (
    .in_1(in_1[3:0]), .in_2(in_2[3:0]), ._8(n4_bit_full_adder_1__8), ._8_75(_11_25[3:0]), .Carry_In(Carry_IN));

  // Notes on the sheet:
  //   8
  //   8.75
  //   .75
  //   10.5
  //   8
  //   8.75
  //   8
  //   .75
endmodule

module _4_bit_full_adder (
  input  [3:0] in_1,
  input  [3:0] in_2,
  input  Carry_In,
  output _8,
  output [3:0] _8_75
);

  wire fa_opt_2_1_carry_bit, FAo2_carry_bit, faopt1_1__4_75;

  FAopt1 _75 (.in_1(faopt1_1__4_75), .in_2(in_1[3]), .Carry(in_2[3]), .S(_8_75[3]), ._4_75(_8));
  FA_opt_2 FAo2 (
    .in_1(fa_opt_2_1_carry_bit), .in_2(in_1[1]), .Carry(in_2[1]), .Carry_Bit(FAo2_carry_bit), ._5_5(_8_75[1]));
  FAopt1 faopt1_1 (.in_1(FAo2_carry_bit), .in_2(in_1[2]), .Carry(in_2[2]), .S(_8_75[2]), ._4_75(faopt1_1__4_75));
  FA_opt_2 fa_opt_2_1 (
    .in_1(in_1[0]), .in_2(in_2[0]), .Carry(Carry_In), .Carry_Bit(fa_opt_2_1_carry_bit), ._5_5(_8_75[0]));

  // Notes on the sheet:
  //   2
  //   Carry
  //   4.75
  //   5.5
  //   .75
  //   2
endmodule

module Logisim_s_Adder (
  input  Carry_In,
  input  [15:0] in_2,
  input  [15:0] in_3,
  output [15:0] out_4,
  output out_5
);

  Adder #(.width(16)) adder_1 (.a(in_2), .b(in_3), .out(out_4), .cin(Carry_In), .cout(out_5));
endmodule

module microarchitecture_1 (
  input  Instruction
);

  wire [15:0] A_Reg, B_Reg, n16bit_car_sel_add_sub_1_out_5;

  Register register_1 ();  // open: D, en, Q, clk, clr
  _16bit_car_sel_add_sub u_16bit_car_sel_add_sub_1 (
    .out_5(n16bit_car_sel_add_sub_1_out_5), .in_3(A_Reg), .in_1(B_Reg), .OP(Instruction));  // open: Overflow
  Register #(.width(16)) register_2 (.D(n16bit_car_sel_add_sub_1_out_5), .Q(A_Reg));  // open: en, clk, clr
  Register #(.width(16)) register_3 (.Q(B_Reg));  // open: D, en, clk, clr
endmodule

module RAM (
  input  in_1,
  input  [15:0] in_2,
  output [15:0] out_3
);

  wire CLK;
  wire [4:0] counter_1_q;
  wire [7:0] ram_1_data;
  wire [15:0] b_reg, n16bit_car_sel_add_sub_1_out_5;

  Counter #(.width(5), .max('h1f)) counter_1 (.Q(counter_1_q), .clk(CLK), .clr(in_1));  // open: load, D, count, carry
  Clock clock_1 (.out(CLK));
  RAM_part #(.addrWidth(5)) ram_1 (.addr(counter_1_q), .data(ram_1_data));  // open: sel, clk, ld, clr
  _16bit_car_sel_add_sub u_16bit_car_sel_add_sub_1 (
    .out_5(n16bit_car_sel_add_sub_1_out_5), .in_3(out_3), .in_1(b_reg), .OP(ram_1_data[0]));  // open: Overflow
  Register #(.width(16)) register_1 (.D(n16bit_car_sel_add_sub_1_out_5), .Q(out_3), .clk(CLK), .clr(in_1));  // open: en
  Register #(.width(16)) register_2 (.D(in_2), .Q(b_reg), .clk(CLK), .clr(in_1));  // open: en

  // Other names for the same wires on the sheet: a_reg[15:0] = out_3; RST = in_1

  // Notes on the sheet:
  //   BREG
endmodule

module More_Instructions (
  input  how_jump_delays,
  input  in_2,
  input  in_3,
  output [15:0] A,
  output [15:0] B,
  output ovfl,
  output [15:0] out_7,
  output Neg
);

  wire and_1_out, and_2_out, CLK, decoder_1_add, decoder_1_ld, decoder_1_sub, decoder_1_xchng, jmp, jmpn, ld,
       lda, not_1_out, or_1_out, or_2_out, or_3_out, or_4_out, or_5_out, or_6_out, or_7_out, register_4_q,
       register_5_q, register_8_q, store, str, undriven, xchg;
  wire [3:0] decoder_1_memory_address, n4_wide_2_1_mux_1_out_4, register_2_q;
  wire [4:0] adr, counter_1_q, jpN_temp, transistor_1_out;
  wire [7:0] Inst_data, ram_1_data;
  wire [15:0] a_regin, ram_2_data, transistor_4_out;

  or or_1 (or_1_out, jmp, jmpn);
  or or_2 (or_2_out, jmpn, jmp);
  Transistor #(.\type ("n"), .width(5)) transistor_1 (.in(jpN_temp), .out(transistor_1_out), .gate(or_2_out));
  not not_1 (not_1_out, or_1_out);
  Counter #(.width(5), .max('h1f)) counter_1 (
    .load(or_1_out), .D(transistor_1_out), .count(not_1_out), .Q(counter_1_q), .clk(CLK), .clr(in_2));  // open: carry
  Clock clock_1 (.out(CLK));
  Hex_Digit_Display hex_digit_display_1 (.value(A[11:8]), .dp(1'b0));
  Hex_Digit_Display hex_digit_display_2 (.value(A[15:12]), .dp(1'b0));
  Hex_Digit_Display hex_digit_display_3 (.value(B[15:12]), .dp(1'b0));
  Hex_Digit_Display hex_digit_display_4 (.value(B[11:8]), .dp(1'b0));
  Hex_Digit_Display hex_digit_display_5 (.value(Inst_data[7:4]), .dp(1'b0));
  Hex_Digit_Display hex_digit_display_6 (.value(A[3:0]), .dp(1'b0));
  Hex_Digit_Display hex_digit_display_7 (.value(A[7:4]), .dp(1'b0));
  Hex_Digit_Display hex_digit_display_8 (.value(B[7:4]), .dp(1'b0));
  Hex_Digit_Display hex_digit_display_9 (.value(B[3:0]), .dp(1'b0));
  Hex_Digit_Display hex_digit_display_10 (.value(Inst_data[3:0]), .dp(1'b0));
  LED led_1 (.in(ovfl));
  Register register_1 (.D(ram_1_data), .Q(Inst_data), .clk(CLK), .clr(in_2));  // open: en
  RAM_part #(.addrWidth(5)) ram_1 (.addr(counter_1_q), .data(ram_1_data));  // open: sel, clk, ld, clr
  _4_wide_2_1_mux u_4_wide_2_1_mux_1 (.A(register_2_q), .B(A[15:12]), .Carry(lda), .out_4(n4_wide_2_1_mux_1_out_4));
  decoder decoder_1 (
    .in_1(Inst_data), .Memory_Address(decoder_1_memory_address), .Add(decoder_1_add), .Sub(decoder_1_sub),
    .ld(decoder_1_ld), .xchng(decoder_1_xchng), .store(str), .jump(jmp), .jump_address(adr), .nop(jmpn),
    .LoadA(lda));  // open: jumpneg
  Hex_Digit_Display hex_digit_display_11 (.value(register_2_q), .dp(1'b0));
  or or_3 (or_3_out, ld, lda);
  Register #(.width(4)) register_2 (
    .D(decoder_1_memory_address), .en(undriven), .Q(register_2_q), .clk(CLK), .clr(in_2));
  and and_1 (and_1_out, how_jump_delays, or_4_out);
  RAM_part #(.addrWidth(4), .dataWidth(16), .bus("separate")) ram_2 (
    .addr(n4_wide_2_1_mux_1_out_4), .din(A), .data(ram_2_data), .str(store), .clk(CLK), .ld(or_3_out),
    .clr(in_3));  // open: sel
  Register #(.width(1)) register_3 (.D(str), .en(undriven), .Q(store), .clk(CLK), .clr(in_2));
  Register #(.width(1)) register_4 (.D(decoder_1_add), .en(undriven), .Q(register_4_q), .clk(CLK), .clr(in_2));
  Register #(.width(1)) register_5 (.D(decoder_1_sub), .en(undriven), .Q(register_5_q), .clk(CLK), .clr(in_2));
  Register #(.width(1)) register_6 (.D(decoder_1_ld), .en(undriven), .Q(ld), .clk(CLK), .clr(in_2));
  Register #(.width(1)) register_7 (.D(decoder_1_xchng), .en(undriven), .Q(xchg), .clk(CLK), .clr(in_2));
  Register #(.width(1)) register_8 (.D(and_1_out), .Q(register_8_q), .clk(CLK), .clr(in_2));  // open: en
  or or_4 (or_4_out, jmpn, jmp);
  _4_0__2_1_mux u_4_0_2_1_mux_1 (.in_1(adr), .in_2(A[4:0]), .out_4(jpN_temp), .in_3(and_2_out));
  and and_2 (and_2_out, jmpn, A[0]);
  or or_5 (or_5_out, register_5_q, register_4_q);
  Hex_Digit_Display hex_digit_display_12 (.value(A[15:12]), .dp(1'b0));
  _16bit_car_sel_add_sub u_16bit_car_sel_add_sub_1 (
    .Overflow(ovfl), .out_5(out_7), .in_3(A), .in_1(B), .OP(register_5_q));
  Transistor #(.\type ("n"), .width(16)) transistor_2 (.in(out_7), .out(a_regin), .gate(or_5_out));
  or or_6 (or_6_out, register_4_q, register_5_q, lda, ld, xchg);
  or or_7 (or_7_out, ld, lda);
  Transistor #(.\type ("n"), .width(16)) transistor_3 (.in(ram_2_data), .out(a_regin), .gate(or_7_out));
  Hex_Digit_Display hex_digit_display_13 (.value(a_regin[3:0]), .dp(1'b0));
  Register #(.width(16)) register_9 (.D(a_regin), .en(or_6_out), .Q(A), .clk(CLK), .clr(in_2));
  Register #(.width(16)) register_10 (.D(transistor_4_out), .en(xchg), .Q(B), .clk(CLK), .clr(in_2));
  Hex_Digit_Display hex_digit_display_14 (.value(a_regin[7:4]), .dp(1'b0));
  Transistor #(.\type ("n"), .width(16)) transistor_4 (.in(A), .out(transistor_4_out), .gate(xchg));
  Hex_Digit_Display hex_digit_display_15 (.value(a_regin[15:12]), .dp(1'b0));
  Hex_Digit_Display hex_digit_display_16 (.value(a_regin[11:8]), .dp(1'b0));
  Transistor #(.\type ("n"), .width(16)) transistor_5 (.in(B), .out(a_regin), .gate(xchg));

  assign Neg = A[0];

  // Other names for the same wires on the sheet: a_reg[15:0] = A; A_adr[3:0] = A[15:12]; b_reg[15:0] = B;
  //   jmp_act = how_jump_delays; RST = in_2; RST_ram = in_3

  // Notes on the sheet:
  //   program counter
  //   Instruction
  //   and
  //   data location
  //   program memory
  //   Store
  //   Ram Addrs
  //   RAM
  //   out of order
  //   Jump Neg
  //   mux
  //   ADD/SUB
  //   OP
  //   OR: xchg, ld, sub, add
  //   areg
  //   breg
  //   load
  //   load A
  //   exchange
endmodule

module decoder (
  input  [7:0] in_1,
  output [3:0] Memory_Address,
  output [4:0] jump_address,
  output Add,
  output Sub,
  output ld,
  output xchng,
  output store,
  output jump,
  output jumpneg,
  output LoadA,
  output nop
);

  nor nor_1 (Add, in_1[0], in_1[1], in_1[2], in_1[3]);
  nor nor_2 (Sub, ~in_1[0], in_1[1], in_1[2], in_1[3]);  // NOR_Gate
  nor nor_3 (ld, in_1[0], ~in_1[1], in_1[2], in_1[3]);  // NOR_Gate
  nor nor_4 (xchng, ~in_1[0], ~in_1[1], in_1[2], in_1[3]);  // NOR_Gate
  nor nor_5 (store, in_1[0], in_1[1], ~in_1[2], in_1[3]);  // NOR_Gate
  nor nor_6 (jump, ~in_1[0], in_1[1], ~in_1[2]);  // NOR_Gate
  nor nor_7 (jumpneg, in_1[0], in_1[1], in_1[2]);
  nor nor_8 (LoadA, ~in_1[0], ~in_1[1], ~in_1[2], in_1[3]);  // NOR_Gate
  nor nor_9 (nop, in_1[0], in_1[1], in_1[2], ~in_1[3]);  // NOR_Gate

  assign jump_address = in_1[7:3];
  assign Memory_Address = in_1[7:4];

  // Notes on the sheet:
  //   Instruction+data
  //   from instruction
  //   its different, and thats ok!
endmodule

module add_sub_logisims (
  input  in_1,
  input  [15:0] in_2,
  input  [15:0] in_3,
  output [15:0] out_4,
  output [15:0] out_5,
  output out_6,
  output out_7
);

  wire adder_1_cout, subtractor_1_bout;
  wire [15:0] adder_1_out, subtractor_1_out, thanks_lojisim_1_out_3;

  thanks_lojisim thanks_lojisim_1 (.in_2(in_2), .in_1(in_1), .out_3(thanks_lojisim_1_out_3));
  Adder #(.width(16)) adder_1 (
    .a(thanks_lojisim_1_out_3), .b(in_3), .out(adder_1_out), .cin(in_1), .cout(adder_1_cout));
  Subtractor #(.width(16)) subtractor_1 (
    .a(thanks_lojisim_1_out_3), .b(thanks_lojisim_1_out_3), .out(subtractor_1_out), .bin(in_1),
    .bout(subtractor_1_bout));
  not not_1 (out_6, subtractor_1_bout);
  Transistor #(.\type ("n")) transistor_1 (.in(out_6), .out(out_7), .gate(in_1));
  Transistor transistor_2 (.in(adder_1_cout), .out(out_7), .gate(in_1));
  Transistor #(.width(16)) transistor_3 (.in(adder_1_out), .out(out_4), .gate(in_1));
  assign out_5 = ~subtractor_1_out;  // NOT_Gate not_2, 16 bits wide
  Transistor #(.\type ("n"), .width(16)) transistor_4 (.in(out_5), .out(out_4), .gate(in_1));

  // Notes on the sheet:
  //   Carry In
endmodule

module _4_0__2_1_mux (
  input  [4:0] in_1,
  input  [4:0] in_2,
  input  in_3,
  output [4:0] out_4
);

  _4to1_Mux u_4to1_mux_1 (.SEL(in_3), .in_2(in_1[0]), .in_3(in_2[0]), .Total_2_75(out_4[0]));
  _4to1_Mux u_4to1_mux_2 (.SEL(in_3), .in_2(in_1[1]), .in_3(in_2[1]), .Total_2_75(out_4[1]));
  _4to1_Mux u_4to1_mux_3 (.SEL(in_3), .in_2(in_1[2]), .in_3(in_2[2]), .Total_2_75(out_4[2]));
  _4to1_Mux u_4to1_mux_4 (.SEL(in_3), .in_2(in_1[3]), .in_3(in_2[3]), .Total_2_75(out_4[3]));
  _4to1_Mux u_4to1_mux_5 (.SEL(in_3), .in_2(in_1[4]), .in_3(in_2[4]), .Total_2_75(out_4[4]));
endmodule
